# Fritzing sketch PCB_4x4_293D (saved by Fritzing 0.8.7b)
circuit board: 24cm x 12cm
breadboards: 1

parts:
  Motor7+11 = Header 4 [package=screwterminal-3.5mm-4_lock]
  Motor7+12 = Header 4 [package=screwterminal-3.5mm-4_lock]
  input_1-6 = Header 4 [package=screwterminal-3.5mm-4_lock]
  293_5 = L293D [package=THT]
  input_1-7 = Header 4 [package=screwterminal-3.5mm-4_lock]
  input_1-8 = Header 4 [package=screwterminal-3.5mm-4_lock]
  293_6 = L293D [package=THT]
  input_1-9 = Header 4 [package=screwterminal-3.5mm-4_lock]
  293_7 = L293D [package=THT]
  293_8 = L293D [package=THT]
  input_1-10 = Header 4 [package=screwterminal-3.5mm-4_lock]
  input_1-11 = Header 4 [package=screwterminal-3.5mm-4_lock]
  Motor7+13 = Header 4 [package=screwterminal-3.5mm-4_lock]
  Motor7+14 = Header 4 [package=screwterminal-3.5mm-4_lock]

nets:
  N1: Motor7+11.1, 293_5.Out_1_(_Controlled_by_Enable_1_)
  N2: Motor7+11.2, 293_5.Out_2_(_Controlled_by_Enable_1_)
  N3: Motor7+11.3, 293_5.Out_3_(_Controlled_by_Enable_2_)
  N4: Motor7+11.4, 293_5.Out_4_(_Controlled_by_Enable_2_)
  N5: Motor7+12.1, 293_6.Out_1_(_Controlled_by_Enable_1_)
  N6: Motor7+12.2, 293_6.Out_2_(_Controlled_by_Enable_1_)
  N7: Motor7+12.3, 293_6.Out_3_(_Controlled_by_Enable_2_)
  N8: Motor7+12.4, 293_6.Out_4_(_Controlled_by_Enable_2_)
  N9: input_1-6.1, 293_5.Enable_1, 293_5.Enable_2, 293_5.+V, input_1-8.1, 293_6.Enable_1, 293_6.Enable_2, 293_6.+V, 293_7.Enable_1, 293_7.Enable_2, 293_7.+V, 293_8.Enable_1, 293_8.Enable_2, 293_8.+V
  N10: input_1-6.2, 293_5.+Vmotor, input_1-8.2, 293_6.+Vmotor, 293_7.+Vmotor, 293_8.+Vmotor
  N11: input_1-6.3, 293_5.0V, input_1-8.3, 293_6.0V, 293_7.0V, 293_8.0V
  N12: 293_5.In_1, input_1-7.1
  N13: 293_5.In_2, input_1-7.2
  N14: 293_5.In_3, input_1-7.3
  N15: 293_5.In_4, input_1-7.4
  N16: 293_6.In_1, input_1-9.1
  N17: 293_6.In_2, input_1-9.2
  N18: 293_6.In_3, input_1-9.3
  N19: 293_6.In_4, input_1-9.4
  N20: 293_7.In_1, input_1-10.1
  N21: 293_7.Out_1_(_Controlled_by_Enable_1_), Motor7+13.1
  N22: 293_7.Out_2_(_Controlled_by_Enable_1_), Motor7+13.2
  N23: 293_7.In_2, input_1-10.2
  N24: 293_7.In_3, input_1-10.3
  N25: 293_7.Out_3_(_Controlled_by_Enable_2_), Motor7+13.3
  N26: 293_7.Out_4_(_Controlled_by_Enable_2_), Motor7+13.4
  N27: 293_7.In_4, input_1-10.4
  N28: 293_8.In_1, input_1-11.1
  N29: 293_8.Out_1_(_Controlled_by_Enable_1_), Motor7+14.1
  N30: 293_8.Out_2_(_Controlled_by_Enable_1_), Motor7+14.2
  N31: 293_8.In_2, input_1-11.2
  N32: 293_8.In_3, input_1-11.3
  N33: 293_8.Out_3_(_Controlled_by_Enable_2_), Motor7+14.3
  N34: 293_8.Out_4_(_Controlled_by_Enable_2_), Motor7+14.4
  N35: 293_8.In_4, input_1-11.4

notes:
  1.5v
  2.12V
  3.ground
