# Fritzing sketch PCB_4x4_595 (saved by Fritzing 0.8.7b)
circuit board: 18cm x 9cm
breadboards: 1

parts:
  U4 = 74HC595 [package="DIP16 [THT]"]
  U5 = 74HC595 [package="DIP16 [THT]"]
  U6 = 74HC595 [package="DIP16 [THT]"]
  U7 = 74HC595 [package="DIP16 [THT]"]
  JP7 = Header 6 [package=1x06-smd]
  JP8 = Header 4 [package=1x04-smd]
  JP9 = Header 4 [package=1x04-smd]
  JP10 = Header 4 [package=1x04-smd]
  JP11 = Header 4 [package=1x04-smd]
  JP12 = Header 4 [package=1x04-smd]
  JP13 = Header 4 [package=1x04-smd]
  JP14 = Header 4 [package=1x04-smd]
  JP15 = Header 4 [package=1x04-smd]
  JP16 = Header 6 [package=1x06-smd]

nets:
  N1: U4.Q1, JP14.2
  N2: U4.Q2, JP14.3
  N3: U4.Q3, JP14.4
  N4: U4.Q4, JP15.1
  N5: U4.Q5, JP15.2
  N6: U4.Q6, JP15.3
  N7: U4.Q7, JP15.4
  GND: U4.GND, U4.OE, U5.GND, U5.OE, U6.GND, U6.OE, U7.GND, U7.OE
  N8: U4.Q7', U5.DS
  VCC: U4.MR, U4.VCC, U5.MR, U5.VCC, U6.MR, U6.VCC, U7.MR, U7.VCC
  N9: U4.SH_CP, U5.SH_CP, U6.SH_CP, U7.SH_CP, JP7.6, JP16.1
  N10: U4.ST_CP, U5.ST_CP, U6.ST_CP, U7.ST_CP, JP7.4, JP16.3
  N11: U4.Q0, JP14.1
  N12: U5.Q1, JP12.2
  N13: U5.Q2, JP12.3
  N14: U5.Q3, JP12.4
  N15: U5.Q4, JP13.1
  N16: U5.Q5, JP13.2
  N17: U5.Q6, JP13.3
  N18: U5.Q7, JP13.4
  N19: U5.Q7', U7.DS
  N20: U5.Q0, JP12.1
  N21: U6.Q1, JP8.2
  N22: U6.Q2, JP8.3
  N23: U6.Q3, JP8.4
  N24: U6.Q4, JP9.1
  N25: U6.Q5, JP9.2
  N26: U6.Q6, JP9.3
  N27: U6.Q7, JP9.4
  N28: U6.DS, U7.Q7'
  N29: U6.Q0, JP8.1
  N30: U7.Q1, JP10.2
  N31: U7.Q2, JP10.3
  N32: U7.Q3, JP10.4
  N33: U7.Q4, JP11.1
  N34: U7.Q5, JP11.2
  N35: U7.Q6, JP11.3
  N36: U7.Q7, JP11.4
  N37: U7.Q0, JP10.1

notes:
  1.clock
  2.data
  3.latch
  4.5V
  5.ground
