# Fritzing sketch SchematicNoduino (saved by Fritzing 0.8.7b)
breadboards: 1

parts:
  293_1 = L293D [package=THT]
  Motor1+2 = Header 4 [package=screwterminal-3.5mm-4_lock]
  C1 = Ceramic Capacitor [capacitance=100nF package="100 mil [THT, multilayer]"]
  C2 = Electrolytic Capacitor [capacitance=1µF package="100 mil [THT, electrolytic]"]
  C3 = Ceramic Capacitor [capacitance=100nF package="100 mil [THT, multilayer]"]
  C4 = Ceramic Capacitor [capacitance=100nF package="100 mil [THT, multilayer]"]
  595_1 = 74HC595 [package="DIP16 [THT]"]
  5Volts = DC Power [voltage=5V]
  12Volts = DC Power [voltage=12V]
  C5 = Ceramic Capacitor [capacitance=100nF package="100 mil [THT, multilayer]"]
  Part1 = Arduino Uno (Rev3)  # not connected

nets:
  N1: 293_1.Enable_1, 293_1.+V, 595_1.MR, 595_1.VCC, 5Volts.V+, C5.0
  N2: 293_1.In_1, 595_1.Q0
  N3: 293_1.Out_1_(_Controlled_by_Enable_1_), Motor1+2.1, C4.0
  GND: 293_1.0V, C1.0, C2.-, C3.1, C4.1, 595_1.OE, 5Volts.V-, 12Volts.V-, C5.1
  N4: 293_1.Out_2_(_Controlled_by_Enable_1_), Motor1+2.2, C3.0
  N5: 293_1.In_2, 595_1.Q1
  N6: 293_1.+Vmotor, 12Volts.V+

notes:
  clock : grey
  data :ochre
  latch: orange
